# Fritzing sketch project (saved by Fritzing 0.9.10b)
breadboards: 1

parts:
  Componente1 = Arduino Uno (Rev3)
  R1 = Resistor [tolerance=±5% power=0.25 resistance=220 package=THT]
  LED1 = smd LED [color="Blue (505nm)" package="0805 [SMD]"]
  LED2 = smd LED [color="Blue (505nm)" package="0805 [SMD]"]
  LED3 = smd LED [color="Blue (505nm)" package="0805 [SMD]"]
  LED4 = smd LED [color="Blue (505nm)" package="0805 [SMD]"]
  LED5 = smd LED [color="Blue (505nm)" package="0805 [SMD]"]
  R2 = Resistor [tolerance=±5% power=0.25 resistance=220 package=THT]
  R3 = Resistor [tolerance=±5% power=0.25 resistance=220 package=THT]
  R4 = Resistor [tolerance=±5% power=0.25 resistance=220 package=THT]
  R5 = Resistor [tolerance=±5% power=0.25 resistance=220 package=THT]

nets:
  N1: Componente1.D8, LED1.anode
  N2: Componente1.D9_PWM, LED2.anode
  N3: Componente1.D10_PWM/SS, LED3.anode
  N4: Componente1.D11_PWM/MOSI, LED4.anode
  N5: Componente1.D12/MISO, LED5.anode
  N6: Componente1.GND, R1.Pin_1, R2.Pin_1, R4.Pin_1, R5.Pin_1
  N7: R1.Pin_0, LED1.cathode
  N8: LED2.cathode, R2.Pin_0
  N9: LED3.cathode, R3.Pin_0
  N10: LED4.cathode, R4.Pin_0
  N11: LED5.cathode, R5.Pin_0
